// Logisim project F5.circ as structural Verilog: 6 circuits, main circuit main
module main (
);

  wire and_1_out, bne, clock, comparator_1_eq, dec_1_is_add, dec_1_is_bner0, dec_1_is_li, or_1_out, undriven,
       undriven_2;
  wire [1:0] dec_1_rd, dec_1_rs1, dec_1_rs2, multiplexer_2_out;
  wire [3:0] dec_1_addr, dec_1_imm;
  wire [7:0] adder_1_out, alu_1_result, bit_extender_1_out, bit_extender_2_out, gpr_1_r0_out, gpr_1_r1_out,
       gpr_1_r2_out, gpr_1_r3_out, gpr_1_rdata1, gpr_1_rdata2, multiplexer_1_out, multiplexer_3_out,
       pc_1_pc_out, rom_1_data;

  Clock clock_1 (.out(clock));
  PC pc_1 (.pc_next(multiplexer_1_out), .WE(1'b1), .clock(undriven), .pc_out(pc_1_pc_out));
  ROM rom_1 (.addr(pc_1_pc_out), .data(rom_1_data));
  Adder adder_1 (.a(pc_1_pc_out), .b(8'h1), .out(adder_1_out));  // open: cin, cout
  Multiplexer #(.width(8)) multiplexer_1 (
    .in0(adder_1_out), .in1(bit_extender_1_out), .out(multiplexer_1_out), .sel(and_1_out));
  dec dec_1 (
    .instr(rom_1_data), .addr(dec_1_addr), .rs2(dec_1_rs2), .rs1(dec_1_rs1), .rd(dec_1_rd),
    .is_add(dec_1_is_add), .is_li(dec_1_is_li), .is_bner0(dec_1_is_bner0), .imm(dec_1_imm));
  assign bit_extender_1_out = {{4{1'b0}}, dec_1_addr};  // Bit_Extender bit_extender_1
  or or_1 (or_1_out, dec_1_is_add, dec_1_is_li);
  Multiplexer #(.width(2)) multiplexer_2 (.in0(dec_1_rs1), .in1(2'b00), .out(multiplexer_2_out), .sel(dec_1_is_bner0));
  assign bit_extender_2_out = {{4{1'b0}}, dec_1_imm};  // Bit_Extender bit_extender_2
  and and_1 (and_1_out, dec_1_is_bner0, bne);
  // Probe on gpr_1_r0_out
  gpr gpr_1 (
    .wdata(multiplexer_3_out), .raddr1(multiplexer_2_out), .waddr(dec_1_rd), .wen(or_1_out),
    .raddr2(dec_1_rs2), .clock(undriven_2), .r0_out(gpr_1_r0_out), .rdata1(gpr_1_rdata1),
    .rdata2(gpr_1_rdata2), .r1_out(gpr_1_r1_out), .r2_out(gpr_1_r2_out), .r3_out(gpr_1_r3_out));
  // Probe on gpr_1_r1_out
  // Probe on gpr_1_r2_out
  // Probe on gpr_1_r3_out
  Comparator comparator_1 (.a(gpr_1_rdata1), .b(gpr_1_rdata2), .eq(comparator_1_eq));  // open: gt, lt
  not not_1 (bne, comparator_1_eq);
  ALU alu_1 (.RegA(gpr_1_rdata1), .RegB(gpr_1_rdata2), .result(alu_1_result));  // open: OE, Carry, Dout
  Multiplexer #(.width(8)) multiplexer_3 (
    .in0(bit_extender_2_out), .in1(alu_1_result), .out(multiplexer_3_out), .sel(dec_1_is_add));

  // Notes on the sheet:
  //   contents of rom_1 (hex, n*v repeats v):
  //   8a 90 a0 b1 17 29 d1 df
endmodule

module gpr (
  input  [7:0] wdata,
  input  [1:0] raddr1,
  input  [1:0] waddr,
  input  wen,
  input  [1:0] raddr2,
  input  clock,
  output [7:0] r0_out,
  output [7:0] rdata1,
  output [7:0] rdata2,
  output [7:0] r1_out,
  output [7:0] r2_out,
  output [7:0] r3_out
);

  wire and_1_out, and_2_out, and_3_out, and_4_out, decoder_1_out0, decoder_1_out1, decoder_1_out2,
       decoder_1_out3;

  Decoder #(.select(2)) decoder_1 (
    .out0(decoder_1_out0), .out1(decoder_1_out1), .out2(decoder_1_out2), .out3(decoder_1_out3), .sel(waddr));  // open: en
  and and_1 (and_1_out, decoder_1_out0, wen);
  and and_2 (and_2_out, decoder_1_out1, wen);
  and and_3 (and_3_out, decoder_1_out2, wen);
  and and_4 (and_4_out, decoder_1_out3, wen);
  Register A0 (.D(wdata), .en(and_1_out), .clk(clock), .Q(r0_out), .clr(1'b0));
  Register A1 (.D(wdata), .en(and_2_out), .clk(clock), .Q(r1_out), .clr(1'b0));
  Register A2 (.D(wdata), .en(and_3_out), .clk(clock), .Q(r2_out), .clr(1'b0));
  Register A3 (.D(wdata), .en(and_4_out), .clk(clock), .Q(r3_out), .clr(1'b0));
  Multiplexer #(.select(2), .width(8)) multiplexer_1 (
    .in0(r0_out), .in1(r1_out), .in2(r2_out), .in3(r3_out), .out(rdata1), .sel(raddr1));
  Multiplexer #(.select(2), .width(8)) multiplexer_2 (
    .in0(r0_out), .in1(r1_out), .in2(r2_out), .in3(r3_out), .out(rdata2), .sel(raddr2));
endmodule

module decorder24 (
  input  A1,
  input  A0,
  output Y0,
  output Y1,
  output Y2,
  output Y3
);

  wire not_1_out, not_2_out;

  not not_1 (not_1_out, A1);
  not not_2 (not_2_out, A0);
  and and_1 (Y0, not_1_out, not_2_out);
  and and_2 (Y1, A1, not_2_out);
  and and_3 (Y2, not_1_out, A0);
  and and_4 (Y3, A1, A0);
endmodule

module dec (
  input  [7:0] instr,
  output [3:0] addr,
  output [1:0] rs2,
  output [1:0] rs1,
  output [1:0] rd,
  output is_add,
  output is_li,
  output is_bner0,
  output [3:0] imm
);

  Decoder #(.select(2)) decoder_1 (.out0(is_add), .out2(is_li), .out3(is_bner0), .sel(instr[7:6]));  // open: out1, en

  assign addr = instr[5:2];
  assign imm = instr[3:0];
  assign rd = instr[5:4];
  assign rs1 = instr[3:2];
  assign rs2 = instr[1:0];
endmodule

module PC (
  input  [7:0] pc_next,
  input  WE,
  input  clock,
  output [7:0] pc_out
);

  Register register_1 (.D(pc_next), .en(WE), .clk(clock), .Q(pc_out), .clr(1'b0));
endmodule

module ALU (
  input  [7:0] RegA,
  input  [7:0] RegB,
  input  OE,
  output [7:0] result,
  output Carry,
  output [7:0] Dout
);

  Adder adder_1 (.a(RegA), .b(RegB), .out(result), .cin(1'b0), .cout(Carry));
  assign Dout = OE ? result : 8'bz;  // Controlled_Buffer controlled_buffer_1
endmodule
