// Logisim project adder4.circ as structural Verilog: 2 circuits, main circuit main
module main (
  input  A0,
  input  B0,
  input  A1,
  input  B1,
  input  A2,
  input  B2,
  input  A3,
  input  B3,
  output S0,
  output S1,
  output S2,
  output S3,
  output Cout
);

  wire fulladder_1_c, fulladder_2_c, fulladder_3_c;

  fulladder fulladder_1 (.A(A0), .B(B0), .Cin(1'b0), .S(S0), .C(fulladder_1_c));
  fulladder fulladder_2 (.A(A1), .B(B1), .Cin(fulladder_1_c), .S(S1), .C(fulladder_2_c));
  fulladder fulladder_3 (.A(A2), .B(B2), .Cin(fulladder_2_c), .S(S2), .C(fulladder_3_c));
  fulladder fulladder_4 (.A(A3), .B(B3), .Cin(fulladder_3_c), .S(S3), .C(Cout));
endmodule

module fulladder (
  input  A,
  input  B,
  input  Cin,
  output S,
  output C
);

  wire and_1_out, and_2_out, xor_1_out;

  xor xor_1 (xor_1_out, A, B);
  xor xor_2 (S, xor_1_out, Cin);
  and and_1 (and_1_out, Cin, xor_1_out);
  and and_2 (and_2_out, A, B);
  or or_1 (C, and_1_out, and_2_out);
endmodule
