// Logisim project and.circ as structural Verilog: 1 circuit, main circuit main
module main (
  input  A,
  input  B,
  output out_3
);

  wire and_1_out;

  and and_1 (and_1_out, A, B);
endmodule
