// Logisim project comparator.circ as structural Verilog: 2 circuits, main circuit main
module main (
  input  A,
  input  B,
  output out_3,
  output out_4,
  output out_5
);

  wire not_1_out, not_2_out, xor_1_out;

  not not_1 (not_1_out, A);
  not not_2 (not_2_out, B);
  and and_1 (out_3, A, not_2_out);
  and and_2 (out_4, not_1_out, B);
  xor xor_1 (xor_1_out, A, B);
  not not_3 (out_5, xor_1_out);
endmodule

module fulladder (
  input  A,
  input  B,
  input  Cin,
  output S,
  output C
);

  wire and_1_out, and_2_out, xor_1_out;

  xor xor_1 (xor_1_out, A, B);
  xor xor_2 (S, xor_1_out, Cin);
  and and_1 (and_1_out, Cin, xor_1_out);
  and and_2 (and_2_out, A, B);
  or or_1 (C, and_1_out, and_2_out);
endmodule
