// Logisim project comparator4.circ as structural Verilog: 2 circuits, main circuit main
module main (
  input  A3,
  input  B3,
  input  A2,
  input  B2,
  input  A1,
  input  B1,
  input  A0,
  input  B0,
  output out_9,
  output out_10,
  output out_11
);

  wire cmp1_1_eq_out, cmp1_1_gt_out, cmp1_1_lt_out, cmp1_2_eq_out, cmp1_2_gt_out, cmp1_2_lt_out,
       cmp1_3_eq_out, cmp1_3_gt_out, cmp1_3_lt_out;

  cmp1 cmp1_1 (
    .A(A3), .B(B3), .GT_in(1'b0), .LT_in(1'b0), .EQ_in(1'b1), .GT_out(cmp1_1_gt_out), .LT_out(cmp1_1_lt_out),
    .EQ_out(cmp1_1_eq_out));
  cmp1 cmp1_2 (
    .A(A2), .B(B2), .GT_in(cmp1_1_gt_out), .LT_in(cmp1_1_lt_out), .EQ_in(cmp1_1_eq_out),
    .GT_out(cmp1_2_gt_out), .LT_out(cmp1_2_lt_out), .EQ_out(cmp1_2_eq_out));
  cmp1 cmp1_3 (
    .A(A1), .B(B1), .GT_in(cmp1_2_gt_out), .LT_in(cmp1_2_lt_out), .EQ_in(cmp1_2_eq_out),
    .GT_out(cmp1_3_gt_out), .LT_out(cmp1_3_lt_out), .EQ_out(cmp1_3_eq_out));
  cmp1 cmp1_4 (
    .A(A0), .B(B0), .GT_in(cmp1_3_gt_out), .LT_in(cmp1_3_lt_out), .EQ_in(cmp1_3_eq_out), .GT_out(out_9),
    .LT_out(out_10), .EQ_out(out_11));
endmodule

module cmp1 (
  input  A,
  input  B,
  input  GT_in,
  input  LT_in,
  input  EQ_in,
  output GT_out,
  output LT_out,
  output EQ_out
);

  wire and_1_out, and_2_out, and_3_out, and_4_out, not_1_out, not_2_out, not_3_out, xor_1_out;

  not not_1 (not_1_out, A);
  not not_2 (not_2_out, B);
  and and_1 (and_1_out, A, not_2_out);
  and and_2 (and_2_out, not_1_out, B);
  xor xor_1 (xor_1_out, A, B);
  not not_3 (not_3_out, xor_1_out);
  and and_3 (and_3_out, not_3_out, GT_in);
  and and_4 (and_4_out, not_3_out, LT_in);
  and and_5 (EQ_out, not_3_out, EQ_in);
  or or_1 (GT_out, and_1_out, and_3_out);
  or or_2 (LT_out, and_2_out, and_4_out);
endmodule
