// Logisim project counter4.circ as structural Verilog: 3 circuits, main circuit main
module main (
  input  enable,
  output [3:0] Q
);

  wire adder4_1_cout, clock_1_out;
  wire [3:0] adder4_1_s0;

  Clock #(.highDuration(4), .lowDuration(4)) clock_1 (.out(clock_1_out));
  Register #(.width(4)) register_1 (.D(adder4_1_s0), .en(enable), .clk(clock_1_out), .Q(Q), .clr(1'b0));
  adder4 adder4_1 (
    .A0(1'b1), .B0(Q[0]), .A1(1'b0), .B1(Q[1]), .A2(1'b0), .B2(Q[2]), .A3(1'b0), .B3(Q[3]),
    .S0(adder4_1_s0[0]), .S1(adder4_1_s0[1]), .S2(adder4_1_s0[2]), .S3(adder4_1_s0[3]), .Cout(adder4_1_cout));
  // also tied to GND on the sheet: adder4_1_cout
endmodule

module fulladder (
  input  A,
  input  B,
  input  Cin,
  output S,
  output C
);

  wire and_1_out, and_2_out, xor_1_out;

  xor xor_1 (xor_1_out, A, B);
  xor xor_2 (S, xor_1_out, Cin);
  and and_1 (and_1_out, Cin, xor_1_out);
  and and_2 (and_2_out, A, B);
  or or_1 (C, and_1_out, and_2_out);
endmodule

module adder4 (
  input  A0,
  input  B0,
  input  A1,
  input  B1,
  input  A2,
  input  B2,
  input  A3,
  input  B3,
  output S0,
  output S1,
  output S2,
  output S3,
  output Cout
);

  wire fulladder_1_c, fulladder_2_c, fulladder_3_c;

  fulladder fulladder_1 (.A(A0), .B(B0), .Cin(1'b0), .S(S0), .C(fulladder_1_c));
  fulladder fulladder_2 (.A(A1), .B(B1), .Cin(fulladder_1_c), .S(S1), .C(fulladder_2_c));
  fulladder fulladder_3 (.A(A2), .B(B2), .Cin(fulladder_2_c), .S(S2), .C(fulladder_3_c));
  fulladder fulladder_4 (.A(A3), .B(B3), .Cin(fulladder_3_c), .S(S3), .C(Cout));
endmodule
