// Logisim project decoder24.circ as structural Verilog: 1 circuit, main circuit main
module main (
  input  A1,
  input  A0,
  output Y0,
  output Y2,
  output Y1,
  output Y3
);

  wire and_1_out, and_2_out, and_3_out, and_4_out, not_1_out, not_2_out;

  not not_1 (not_1_out, A1);
  not not_2 (not_2_out, A0);
  and and_1 (and_1_out, not_1_out, not_2_out);
  and and_2 (and_2_out, A1, not_2_out);
  and and_3 (and_3_out, not_1_out, A0);
  and and_4 (and_4_out, A1, A0);
endmodule
