// Logisim project dff.circ as structural Verilog: 1 circuit, main circuit main
module main (
  input  D,
  output Q
);

  wire clock_1_out;

  D_Flip_Flop d_ff_1 (.D(D), .clk(clock_1_out), .Q(Q));  // open: Qn, preset, reset
  Clock clock_1 (.out(clock_1_out));
endmodule
