// Logisim project or.circ as structural Verilog: 1 circuit, main circuit main
module main (
  input  A,
  input  B,
  output out_3
);

  wire or_1_out;

  or or_1 (or_1_out, A, B);
endmodule
