// Logisim project ram44.circ as structural Verilog: 3 circuits, main circuit main
module main (
  input  WE,
  input  [1:0] addr,
  input  [3:0] Din,
  output [3:0] Dout
);

  wire and_1_out, and_2_out, and_3_out, and_4_out, clock_1_out, decorder24_1_y0, decorder24_1_y1,
       decorder24_1_y2, decorder24_1_y3;
  wire [3:0] mux41_1_p3, mux41_1_p4, mux41_1_p5, mux41_1_p6;

  decorder24 decorder24_1 (
    .A1(addr[0]), .A0(addr[1]), .Y0(decorder24_1_y0), .Y1(decorder24_1_y1), .Y2(decorder24_1_y2),
    .Y3(decorder24_1_y3));
  // mux41 mux41_1: pin names not known; wires that end beside it: addr[0], addr[1], mux41_1_p3, mux41_1_p4, mux41_1_p5, mux41_1_p6, Dout
  and and_1 (and_1_out, WE, decorder24_1_y0);
  and and_2 (and_2_out, WE, decorder24_1_y1);
  and and_3 (and_3_out, WE, decorder24_1_y2);
  and and_4 (and_4_out, WE, decorder24_1_y3);
  Clock clock_1 (.out(clock_1_out));
  Register #(.width(4)) register_1 (.D(Din), .en(and_1_out), .clk(clock_1_out), .Q(mux41_1_p3), .clr(1'b0));
  Register #(.width(4)) register_2 (.D(Din), .en(and_2_out), .clk(clock_1_out), .Q(mux41_1_p4), .clr(1'b0));
  Register #(.width(4)) register_3 (.D(Din), .en(and_3_out), .clk(clock_1_out), .Q(mux41_1_p5), .clr(1'b0));
  Register #(.width(4)) register_4 (.D(Din), .en(and_4_out), .clk(clock_1_out), .Q(mux41_1_p6), .clr(1'b0));
endmodule

module decorder24 (
  input  A1,
  input  A0,
  output Y0,
  output Y1,
  output Y2,
  output Y3
);

  wire not_1_out, not_2_out;

  not not_1 (not_1_out, A1);
  not not_2 (not_2_out, A0);
  and and_1 (Y0, not_1_out, not_2_out);
  and and_2 (Y1, A1, not_2_out);
  and and_3 (Y2, not_1_out, A0);
  and and_4 (Y3, A1, A0);
endmodule

module mux41 (
  input  [3:0] S1,
  input  [3:0] S0,
  input  [3:0] D0,
  input  [3:0] D1,
  input  [3:0] D2,
  input  [3:0] D3,
  output [3:0] Y
);

  wire [3:0] and_1_out, and_2_out, and_3_out, and_4_out, not_1_out, not_2_out;

  assign not_1_out = ~S1;  // NOT_Gate not_1, 4 bits wide
  assign not_2_out = ~S0;  // NOT_Gate not_2, 4 bits wide
  assign and_1_out = not_1_out & not_2_out & D0;  // AND_Gate and_1, 4 bits wide
  assign and_2_out = not_1_out & D1;  // AND_Gate and_2, 4 bits wide
  assign and_3_out = S1 & not_2_out & D2;  // AND_Gate and_3, 4 bits wide
  assign and_4_out = S1 & S0 & D3;  // AND_Gate and_4, 4 bits wide
  assign Y = and_1_out | and_2_out | and_3_out | and_4_out;  // OR_Gate or_1, 4 bits wide
endmodule
