// Logisim project ram84.circ as structural Verilog: 1 circuit, main circuit main
module main (
  input  [2:0] Addr,
  input  WE,
  input  [3:0] Din,
  output [3:0] Dout
);

  wire clock_1_out;

  Clock clock_1 (.out(clock_1_out));
  RAM #(.addrWidth(3), .dataWidth(4)) ram_1 (
    .addr(Addr), .we(WE), .oe(1'b1), .clk(clock_1_out), .din(Din), .dout(Dout));
endmodule
