// Logisim project register4.circ as structural Verilog: 1 circuit, main circuit main
module main (
  input  [3:0] D,
  input  enable,
  output [3:0] Q
);

  wire clock_1_out;

  Clock clock_1 (.out(clock_1_out));
  Register #(.width(4)) register_1 (.D(D), .en(enable), .clk(clock_1_out), .Q(Q), .clr(1'b0));
endmodule
