// Logisim project sCPU.circ as structural Verilog: 4 circuits, main circuit main
module main (
);

  wire and_1_out, and_2_out, and_3_out, and_4_out, and_5_out, clock_1_out, clock_2_out, decorder24_1_y0,
       decorder24_1_y1, decorder24_1_y2, decorder24_1_y3, not_1_out;
  wire [7:0] adder_1_out, bit_extender_1_out, register_1_q, register_2_q, register_3_q, register_4_q,
       register_5_q, rom_1_data;

  Clock clock_1 (.out(clock_1_out));
  Register register_1 (.D(adder_1_out), .en(1'b1), .clk(clock_1_out), .Q(register_1_q));  // open: clr
  ROM rom_1 (.addr(register_1_q), .data(rom_1_data));
  Adder adder_1 (.a(register_1_q), .b(8'h1), .out(adder_1_out), .cin(1'b0));  // open: cout
  assign bit_extender_1_out = {{4{1'b0}}, rom_1_data[3:0]};  // Bit_Extender bit_extender_1
  not not_1 (not_1_out, rom_1_data[6]);
  and and_1 (and_1_out, not_1_out, rom_1_data[7]);
  decorder24 decorder24_1 (
    .A1(rom_1_data[5]), .A0(rom_1_data[4]), .Y0(decorder24_1_y0), .Y1(decorder24_1_y1), .Y2(decorder24_1_y2),
    .Y3(decorder24_1_y3));
  and and_2 (and_2_out, decorder24_1_y0, and_1_out);
  and and_3 (and_3_out, decorder24_1_y1, and_1_out);
  and and_4 (and_4_out, decorder24_1_y2, and_1_out);
  and and_5 (and_5_out, decorder24_1_y3, and_1_out);
  Clock clock_2 (.out(clock_2_out));
  Register register_2 (.D(bit_extender_1_out), .en(and_2_out), .clk(clock_2_out), .Q(register_2_q));  // open: clr
  Register register_3 (.D(bit_extender_1_out), .en(and_3_out), .clk(clock_2_out), .Q(register_3_q));  // open: clr
  Register register_4 (.D(bit_extender_1_out), .en(and_4_out), .clk(clock_2_out), .Q(register_4_q));  // open: clr
  Register register_5 (.D(bit_extender_1_out), .en(and_5_out), .clk(clock_2_out), .Q(register_5_q));  // open: clr
  // Probe on register_2_q
  // Probe on register_3_q
  // Probe on register_4_q
  // Probe on register_5_q

  // Notes on the sheet:
  //   contents of rom_1 (hex, n*v repeats v):
  //   85 93 a7 b1 27*0 10
endmodule

module decorder24 (
  input  A1,
  input  A0,
  output Y0,
  output Y1,
  output Y2,
  output Y3
);

  wire not_1_out, not_2_out;

  not not_1 (not_1_out, A1);
  not not_2 (not_2_out, A0);
  and and_1 (Y0, not_1_out, not_2_out);
  and and_2 (Y1, A1, not_2_out);
  and and_3 (Y2, not_1_out, A0);
  and and_4 (Y3, A1, A0);
endmodule

module fulladder (
  input  A,
  input  B,
  input  Cin,
  output S,
  output C
);

  wire and_1_out, and_2_out, xor_1_out;

  xor xor_1 (xor_1_out, A, B);
  xor xor_2 (S, xor_1_out, Cin);
  and and_1 (and_1_out, Cin, xor_1_out);
  and and_2 (and_2_out, A, B);
  or or_1 (C, and_1_out, and_2_out);
endmodule

module adder4 (
  input  A0,
  input  B0,
  input  A1,
  input  B1,
  input  A2,
  input  B2,
  input  A3,
  input  B3,
  output S0,
  output S1,
  output S2,
  output S3,
  output Cout
);

  wire fulladder_1_c, fulladder_2_c, fulladder_3_c;

  fulladder fulladder_1 (.A(A0), .B(B0), .Cin(1'b0), .S(S0), .C(fulladder_1_c));
  fulladder fulladder_2 (.A(A1), .B(B1), .Cin(fulladder_1_c), .S(S1), .C(fulladder_2_c));
  fulladder fulladder_3 (.A(A2), .B(B2), .Cin(fulladder_2_c), .S(S2), .C(fulladder_3_c));
  fulladder fulladder_4 (.A(A3), .B(B3), .Cin(fulladder_3_c), .S(S3), .C(Cout));
endmodule
