// Logisim project sCPU3.circ as structural Verilog: 5 circuits, main circuit main
module main (
);

  wire add_en, and_3_out, and_4_out, and_5_out, and_6_out, clk, decorder24_1_y0, decorder24_1_y1,
       decorder24_1_y2, decorder24_1_y3, li_en, not_1_out, not_2_out, wen;
  wire [1:0] rom_1_data, rom_1_data_2;
  wire [7:0] adder_1_out, adder_2_cout, bit_extender_1_out, multiplexer_1_out, rd_1, rd_2, register_1_q,
       register_2_q, register_3_q, register_4_q, register_5_q;
  wire [7:4] rom_1_data_3;

  Clock clock_1 (.out(clk));
  Register register_1 (.D(adder_1_out), .en(1'b1), .clk(clk), .Q(register_1_q));  // open: clr
  ROM rom_1 (.addr(register_1_q), .data({rom_1_data_3, rom_1_data_2, rom_1_data}));
  Adder adder_1 (.a(register_1_q), .b(8'h1), .out(adder_1_out), .cin(1'b0));  // open: cout
  Adder adder_2 (.a(rd_1), .b(rd_2), .cin(1'b0), .cout(adder_2_cout[0]));  // open: out
  Multiplexer #(.width(8)) multiplexer_1 (
    .in0(adder_2_cout), .in1(bit_extender_1_out), .out(multiplexer_1_out), .sel(li_en));
  assign bit_extender_1_out = {{4{1'b0}}, {rom_1_data_2, rom_1_data}};  // Bit_Extender bit_extender_1
  not not_1 (not_1_out, rom_1_data_3[6]);
  and and_1 (li_en, not_1_out, rom_1_data_3[7]);
  not not_2 (not_2_out, rom_1_data_3[7]);
  decorder24 decorder24_1 (
    .A1(rom_1_data_3[5]), .A0(rom_1_data_3[4]), .Y0(decorder24_1_y0), .Y1(decorder24_1_y1),
    .Y2(decorder24_1_y2), .Y3(decorder24_1_y3));
  and and_2 (add_en, not_2_out, not_1_out);
  or or_1 (wen, li_en, add_en);
  and and_3 (and_3_out, decorder24_1_y0, wen);
  and and_4 (and_4_out, decorder24_1_y1, wen);
  and and_5 (and_5_out, decorder24_1_y2, wen);
  and and_6 (and_6_out, decorder24_1_y3, wen);
  Register register_2 (.D(multiplexer_1_out), .en(and_3_out), .clk(clk), .Q(register_2_q), .clr(1'b0));
  Register register_3 (.D(multiplexer_1_out), .en(and_4_out), .clk(clk), .Q(register_3_q), .clr(1'b0));
  Register register_4 (.D(multiplexer_1_out), .en(and_5_out), .clk(clk), .Q(register_4_q), .clr(1'b0));
  Register register_5 (.D(multiplexer_1_out), .en(and_6_out), .clk(clk), .Q(register_5_q), .clr(1'b0));
  // Probe on register_2_q
  // Probe on register_3_q
  // Probe on register_4_q
  // Probe on register_5_q
  Multiplexer #(.select(2), .width(8)) multiplexer_2 (
    .in0(register_2_q), .in1(register_3_q), .in2(register_4_q), .in3(register_5_q), .out(rd_1),
    .sel(rom_1_data));
  Multiplexer #(.select(2), .width(8)) multiplexer_3 (
    .in0(register_2_q), .in1(register_3_q), .in2(register_4_q), .in3(register_5_q), .out(rd_2),
    .sel(rom_1_data_2));
  // Pins of 1 and 8 bits meet at adder_2_cout

  // Notes on the sheet:
  //   contents of rom_1 (hex, n*v repeats v):
  //   8a 90 a0 b1 17 29 d1 df 23*0 10
endmodule

module decorder24 (
  input  A1,
  input  A0,
  output Y0,
  output Y1,
  output Y2,
  output Y3
);

  wire not_1_out, not_2_out;

  not not_1 (not_1_out, A1);
  not not_2 (not_2_out, A0);
  and and_1 (Y0, not_1_out, not_2_out);
  and and_2 (Y1, A1, not_2_out);
  and and_3 (Y2, not_1_out, A0);
  and and_4 (Y3, A1, A0);
endmodule

module fulladder (
  input  A,
  input  B,
  input  Cin,
  output S,
  output C
);

  wire and_1_out, and_2_out, xor_1_out;

  xor xor_1 (xor_1_out, A, B);
  xor xor_2 (S, xor_1_out, Cin);
  and and_1 (and_1_out, Cin, xor_1_out);
  and and_2 (and_2_out, A, B);
  or or_1 (C, and_1_out, and_2_out);
endmodule

module adder4 (
  input  A0,
  input  B0,
  input  A1,
  input  B1,
  input  A2,
  input  B2,
  input  A3,
  input  B3,
  output S0,
  output S1,
  output S2,
  output S3,
  output Cout
);

  wire fulladder_1_c, fulladder_2_c, fulladder_3_c;

  fulladder fulladder_1 (.A(A0), .B(B0), .Cin(1'b0), .S(S0), .C(fulladder_1_c));
  fulladder fulladder_2 (.A(A1), .B(B1), .Cin(fulladder_1_c), .S(S1), .C(fulladder_2_c));
  fulladder fulladder_3 (.A(A2), .B(B2), .Cin(fulladder_2_c), .S(S2), .C(fulladder_3_c));
  fulladder fulladder_4 (.A(A3), .B(B3), .Cin(fulladder_3_c), .S(S3), .C(Cout));
endmodule

module mux41 (
  input  [7:0] S1,
  input  [7:0] S0,
  input  [7:0] D0,
  input  [7:0] D1,
  input  [7:0] D2,
  input  [7:0] D3,
  output [7:0] Y
);

  wire [7:0] and_1_out, and_2_out, and_3_out, and_4_out, not_1_out, not_2_out;

  assign not_1_out = ~S1;  // NOT_Gate not_1, 8 bits wide
  assign not_2_out = ~S0;  // NOT_Gate not_2, 8 bits wide
  assign and_1_out = not_1_out & not_2_out & D0;  // AND_Gate and_1, 8 bits wide
  assign and_2_out = not_1_out & S1 & D1;  // AND_Gate and_2, 8 bits wide
  assign and_3_out = S0 & not_2_out & D2;  // AND_Gate and_3, 8 bits wide
  assign and_4_out = S1 & S0 & D3;  // AND_Gate and_4, 8 bits wide
  assign Y = and_1_out | and_2_out | and_3_out | and_4_out;  // OR_Gate or_1, 8 bits wide
endmodule
