// Logisim project try.circ as structural Verilog: 11 circuits, main circuit main
module main (
  input  WE3,
  input  [7:0] test,
  input  OE4,
  input  OE,
  input  WE2,
  input  WE4,
  input  OE5,
  input  OE3,
  input  WE0,
  input  OE0,
  input  OE2,
  input  WE1,
  input  OE1,
  output [7:0] Reg2,
  output [7:0] MBR,
  output [7:0] Reg0,
  output [7:0] Dout,
  output [7:0] result,
  output Carry,
  output [7:0] Reg1
);

  wire clock;
  wire [3:0] MAR_store;
  wire [7:0] alu_1_dout, IR_store, RegA_dout, RegB_dout, RegC_store;

  Button button_1 (.out(clock));
  register_8 IR (.Din(RegC_store), .WE(WE3), .OE(OE4), .Clock(clock), .store(IR_store), .Dout(Reg2));
  register_8 RegA (.Din(RegC_store), .WE(WE0), .OE(OE0), .Clock(clock), .store(Reg0), .Dout(RegA_dout));
  register_8 RegB (.Din(RegC_store), .WE(WE1), .OE(OE1), .Clock(clock), .store(Reg1), .Dout(RegB_dout));
  ALU alu_1 (.RegA(RegA_dout), .RegB(RegB_dout), .OE(OE2), .result(result), .Dout(alu_1_dout), .Carry(Carry));
  register_4 MAR (.Din(IR_store[3:0]), .store(MAR_store));  // open: We, OE, Clock, Dout
  register_8 RegC (.Din(alu_1_dout), .WE(WE2), .OE(OE3), .Clock(clock), .store(RegC_store), .Dout(Dout));
  assign RegC_store = OE ? test : 8'bz;  // Controlled_Buffer controlled_buffer_1
  register_8 register_8_1 (.Din(RegC_store), .WE(WE4), .OE(OE5), .Clock(clock), .store(MBR), .Dout(RegC_store));
endmodule

module halfadder (
  input  A,
  input  B,
  output Sum,
  output Carry
);

  xor xor_1 (Sum, A, B);
  and and_1 (Carry, A, B);
endmodule

module fulladder (
  input  C,
  input  A,
  input  B,
  output Sum,
  output Carry
);

  wire halfadder_1_carry, halfadder_1_sum, halfadder_2_carry;

  halfadder halfadder_1 (.A(A), .B(B), .Sum(halfadder_1_sum), .Carry(halfadder_1_carry));
  halfadder halfadder_2 (.A(C), .B(halfadder_1_sum), .Sum(Sum), .Carry(halfadder_2_carry));
  or or_1 (Carry, halfadder_2_carry, halfadder_1_carry);
endmodule

module adder8 (
  input  [7:0] A,
  input  [7:0] B,
  output [7:0] Sum,
  output Carry
);

  wire fulladder_1_carry, fulladder_2_carry, fulladder_3_carry, fulladder_4_carry, fulladder_5_carry,
       fulladder_6_carry, halfadder_1_carry;

  halfadder halfadder_1 (.A(A[0]), .B(B[0]), .Sum(Sum[0]), .Carry(halfadder_1_carry));
  fulladder fulladder_1 (.C(halfadder_1_carry), .A(A[1]), .B(B[1]), .Sum(Sum[1]), .Carry(fulladder_1_carry));
  fulladder fulladder_2 (.C(fulladder_1_carry), .A(A[2]), .B(B[2]), .Sum(Sum[2]), .Carry(fulladder_2_carry));
  fulladder fulladder_3 (.C(fulladder_2_carry), .A(A[3]), .B(B[3]), .Sum(Sum[3]), .Carry(fulladder_3_carry));
  fulladder fulladder_4 (.C(fulladder_3_carry), .A(A[4]), .B(B[4]), .Sum(Sum[4]), .Carry(fulladder_4_carry));
  fulladder fulladder_5 (.C(fulladder_4_carry), .A(A[5]), .B(B[5]), .Sum(Sum[5]), .Carry(fulladder_5_carry));
  fulladder fulladder_6 (.C(fulladder_5_carry), .A(A[6]), .B(B[6]), .Sum(Sum[6]), .Carry(fulladder_6_carry));
  fulladder fulladder_7 (.C(fulladder_6_carry), .A(A[7]), .B(B[7]), .Sum(Sum[7]), .Carry(Carry));
endmodule

module register8 (
  input  [7:0] Din,
  input  WE,
  input  OE,
  input  Clock,
  output [7:0] store,
  output [7:0] Dout
);

  Register register_1 (.D(Din), .en(WE), .clk(Clock), .Q(store));  // open: clr
  assign Dout = OE ? store : 8'bz;  // Controlled_Buffer controlled_buffer_1
endmodule

module memory_cell (
  input  Din,
  input  str,
  input  column,
  input  row,
  input  ld,
  output Dout
);

  wire and_1_out, and_2_out, and_3_out, register_1_q;

  and and_1 (and_1_out, column, row);
  and and_2 (and_2_out, str, and_1_out);
  Register #(.width(1)) register_1 (.D(Din), .en(and_2_out), .Q(register_1_q));  // open: clk, clr
  and and_3 (and_3_out, ld, and_1_out);
  assign Dout = and_3_out ? register_1_q : 1'bz;  // Controlled_Buffer controlled_buffer_1
endmodule

module memory16 (
  input  Din,
  input  [3:0] in_2,
  input  str,
  input  ld,
  output Dout
);

  wire [7:0] rom_1_data;

  ROM #(.addrWidth(4)) rom_1 (.addr(in_2), .data(rom_1_data));
  memory_cell memory_cell_1 (.Din(Din), .str(str), .column(rom_1_data[1]), .row(rom_1_data[0]), .ld(ld), .Dout(Dout));
  memory_cell memory_cell_2 (.Din(Din), .str(str), .column(rom_1_data[1]), .row(rom_1_data[2]), .ld(ld), .Dout(Dout));
  memory_cell memory_cell_3 (.Din(Din), .str(str), .column(rom_1_data[1]), .row(rom_1_data[4]), .ld(ld), .Dout(Dout));
  memory_cell memory_cell_4 (.Din(Din), .str(str), .column(rom_1_data[1]), .row(rom_1_data[6]), .ld(ld), .Dout(Dout));
  memory_cell memory_cell_5 (.Din(Din), .str(str), .column(rom_1_data[3]), .row(rom_1_data[0]), .ld(ld), .Dout(Dout));
  memory_cell memory_cell_6 (.Din(Din), .str(str), .column(rom_1_data[3]), .row(rom_1_data[2]), .ld(ld), .Dout(Dout));
  memory_cell memory_cell_7 (.Din(Din), .str(str), .column(rom_1_data[3]), .row(rom_1_data[4]), .ld(ld), .Dout(Dout));
  memory_cell memory_cell_8 (.Din(Din), .str(str), .column(rom_1_data[3]), .row(rom_1_data[6]), .ld(ld), .Dout(Dout));
  memory_cell memory_cell_9 (.Din(Din), .str(str), .column(rom_1_data[5]), .row(rom_1_data[0]), .ld(ld), .Dout(Dout));
  memory_cell memory_cell_10 (.Din(Din), .str(str), .column(rom_1_data[5]), .row(rom_1_data[2]), .ld(ld), .Dout(Dout));
  memory_cell memory_cell_11 (.Din(Din), .str(str), .column(rom_1_data[5]), .row(rom_1_data[4]), .ld(ld), .Dout(Dout));
  memory_cell memory_cell_12 (.Din(Din), .str(str), .column(rom_1_data[5]), .row(rom_1_data[6]), .ld(ld), .Dout(Dout));
  memory_cell memory_cell_13 (.Din(Din), .str(str), .column(rom_1_data[7]), .row(rom_1_data[0]), .ld(ld), .Dout(Dout));
  memory_cell memory_cell_14 (.Din(Din), .str(str), .column(rom_1_data[7]), .row(rom_1_data[2]), .ld(ld), .Dout(Dout));
  memory_cell memory_cell_15 (.Din(Din), .str(str), .column(rom_1_data[7]), .row(rom_1_data[4]), .ld(ld), .Dout(Dout));
  memory_cell memory_cell_16 (.Din(Din), .str(str), .column(rom_1_data[7]), .row(rom_1_data[6]), .ld(ld), .Dout(Dout));
endmodule

module register_8 (
  input  [7:0] Din,
  input  WE,
  input  OE,
  input  Clock,
  output [7:0] store,
  output [7:0] Dout
);

  register8 register8_1 (.Din(Din), .WE(WE), .OE(OE), .Clock(Clock), .store(store), .Dout(Dout));
endmodule

module register4 (
  input  [3:0] Din,
  input  WE,
  input  OE,
  input  Clock,
  output [3:0] store,
  output [3:0] Dout
);

  Register #(.width(4)) register_1 (.D(Din), .en(WE), .clk(Clock), .Q(store));  // open: clr
  assign Dout = OE ? store : 4'bz;  // Controlled_Buffer controlled_buffer_1
endmodule

module register_4 (
  input  [3:0] Din,
  input  We,
  input  OE,
  input  Clock,
  output [3:0] store,
  output [3:0] Dout
);

  register4 register4_1 (.Din(Din), .WE(We), .OE(OE), .Clock(Clock), .store(store), .Dout(Dout));
endmodule

module ALU (
  input  [7:0] RegA,
  input  [7:0] RegB,
  input  OE,
  output [7:0] result,
  output [7:0] Dout,
  output Carry
);

  Adder adder_1 (.a(RegA), .b(RegB), .out(result), .cin(1'b0), .cout(Carry));
  assign Dout = OE ? result : 8'bz;  // Controlled_Buffer controlled_buffer_1
endmodule
