// Logisim project wholeF6.circ as structural Verilog: 7 circuits, main circuit main
module main (
  input  sw0,
  input  sw1,
  input  sw2,
  input  btn0,
  input  sw3,
  input  bnt1,
  input  sw4,
  input  btn2,
  input  sw5,
  input  btn3,
  input  sw6,
  input  btn4,
  input  sw7,
  input  btn5,
  input  btn6,
  input  btn7
);

  wire and_1_out, and_2_out, bne, clock, comparator_1_eq, dec_1_io_dir, dec_1_is_li, nor_1_out, not_1_out,
       or_1_out, s1, seg7_rom_1_a, seg7_rom_1_b, seg7_rom_1_c, seg7_rom_1_d, seg7_rom_1_e, seg7_rom_1_f,
       seg7_rom_1_g;
  wire [0:0] dec_1_is_add;
  wire [1:0] dec_1_imm, dec_1_is_bner0, dec_1_rd, dec_1_rs1, dec_1_rs2, dec_1_s, multiplexer_2_out;
  wire [2:0] dec_1_idx;
  wire [3:0] dec_1_offset;
  wire [7:0] adder_1_out, alu_1_result, bit_extender_1_out, bit_extender_2_out, gpr_1_r0_out, gpr_1_r1_out,
       gpr_1_r2_out, gpr_1_r3_out, gpr_1_rdata1, gpr_1_rdata2, led_reg_q, multiplexer_1_out,
       multiplexer_3_out, multiplexer_4_out, pc_1_pc_out, register_1_q, rom_1_data, shifter_1_out;

  Clock clock_1 (.out(clock));
  PC pc_1 (.pc_next(adder_1_out), .WE(1'b1), .clock(clock), .pc_out(pc_1_pc_out));
  Multiplexer #(.width(8)) multiplexer_1 (
    .in0(8'h1), .in1(bit_extender_1_out), .out(multiplexer_1_out), .sel(and_1_out));
  ROM rom_1 (.addr(pc_1_pc_out), .data(rom_1_data));
  Adder adder_1 (.a(pc_1_pc_out), .b(multiplexer_1_out), .out(adder_1_out));  // open: cin, cout
  dec dec_1 (
    .instr(rom_1_data), .offset(dec_1_offset), .rs2(dec_1_rs2), .rs1(dec_1_rs1), .rd(dec_1_rd),
    .is_add(dec_1_is_add[0]), .is_io(dec_1_is_bner0[1]), .is_li(dec_1_is_li), .imm(dec_1_imm),
    .is_bner0(dec_1_is_bner0[0]), .s(dec_1_s), .idx(dec_1_idx), .io_dir(dec_1_io_dir));
  assign bit_extender_1_out = {{4{dec_1_offset[3]}}, dec_1_offset};  // Bit_Extender bit_extender_1
  nor nor_1 (nor_1_out, dec_1_idx[0], dec_1_idx[1], dec_1_idx[2]);
  or or_1 (or_1_out, dec_1_is_add[0], dec_1_is_li, s1);
  Multiplexer #(.select(2), .width(2)) multiplexer_2 (
    .in0(dec_1_rs1), .in1(2'b00), .in2(dec_1_rd), .in3(2'b00), .out(multiplexer_2_out), .sel(dec_1_is_bner0));
  assign bit_extender_2_out = {{6{1'b0}}, dec_1_imm};  // Bit_Extender bit_extender_2
  and and_1 (and_1_out, dec_1_is_bner0[0], bne);
  and and_2 (and_2_out, dec_1_is_bner0[1], dec_1_io_dir, nor_1_out);
  Multiplexer #(.width(8)) multiplexer_3 (
    .in0({sw7, sw6, sw5, sw4, sw3, sw2, sw1, sw0}), .in1({btn7, btn6, btn5, btn4, btn3, btn2, bnt1, btn0}),
    .out(multiplexer_3_out), .sel(dec_1_idx[0]));
  Register led_reg (.D(gpr_1_rdata1), .en(and_2_out), .clk(clock), .Q(led_reg_q), .clr(1'b0));
  // Probe on gpr_1_r0_out
  gpr gpr_1 (
    .wdata(multiplexer_4_out), .raddr1(multiplexer_2_out), .waddr(dec_1_rd), .wen(or_1_out),
    .raddr2(dec_1_rs2), .clock(clock), .r0_out(gpr_1_r0_out), .rdata1(gpr_1_rdata1), .rdata2(gpr_1_rdata2),
    .r1_out(gpr_1_r1_out), .r2_out(gpr_1_r2_out), .r3_out(gpr_1_r3_out));
  // Probe on gpr_1_r1_out
  // Probe on gpr_1_r2_out
  // Probe on gpr_1_r3_out
  Shifter shifter_1 (.in(bit_extender_2_out), .\dist ({dec_1_s, 1'b0}), .out(shifter_1_out));
  LED led_1 (.in(led_reg_q[0]));
  LED led_2 (.in(led_reg_q[1]));
  LED led_3 (.in(led_reg_q[2]));
  LED led_4 (.in(led_reg_q[3]));
  LED led_5 (.in(led_reg_q[4]));
  LED led_6 (.in(led_reg_q[5]));
  LED led_7 (.in(led_reg_q[6]));
  LED led_8 (.in(led_reg_q[7]));
  Comparator comparator_1 (.a(gpr_1_rdata1), .b(gpr_1_rdata2), .eq(comparator_1_eq));  // open: gt, lt
  not not_1 (not_1_out, dec_1_io_dir);
  not not_2 (bne, comparator_1_eq);
  and and_3 (s1, dec_1_is_bner0[1], not_1_out);
  Register register_1 (.D(gpr_1_rdata1), .en(and_2_out), .clk(clock), .Q(register_1_q), .clr(1'b0));
  ALU alu_1 (.RegA(gpr_1_rdata1), .RegB(gpr_1_rdata2), .result(alu_1_result));  // open: OE, Carry, Dout
  Multiplexer #(.select(2), .width(8)) multiplexer_4 (
    .in0(shifter_1_out), .in1(alu_1_result), .in2(multiplexer_3_out), .in3({8{1'b0}}),
    .out(multiplexer_4_out), .sel({s1, dec_1_is_add[0]}));
  seg7_rom seg7_rom_1 (
    .in_1(register_1_q[3:0]), .a(seg7_rom_1_a), .b(seg7_rom_1_b), .c(seg7_rom_1_c), .d(seg7_rom_1_d),
    .e(seg7_rom_1_e), .f(seg7_rom_1_f), .g(seg7_rom_1_g));
  _7_Segment_Display u_7_segment_display_1 (
    .g(seg7_rom_1_a), .f(seg7_rom_1_b), .a(seg7_rom_1_d), .b(seg7_rom_1_f), .e(seg7_rom_1_c),
    .d(seg7_rom_1_e), .c(seg7_rom_1_g));  // open: dp

  // Notes on the sheet:
  //   contents of rom_1 (hex, n*v repeats v):
  //   40 48 49 f7
endmodule

module gpr (
  input  [7:0] wdata,
  input  [1:0] raddr1,
  input  [1:0] waddr,
  input  wen,
  input  [1:0] raddr2,
  input  clock,
  output [7:0] r0_out,
  output [7:0] rdata1,
  output [7:0] rdata2,
  output [7:0] r1_out,
  output [7:0] r2_out,
  output [7:0] r3_out
);

  wire and_1_out, and_2_out, and_3_out, and_4_out, decoder_1_out0, decoder_1_out1, decoder_1_out2,
       decoder_1_out3;

  Decoder #(.select(2)) decoder_1 (
    .out0(decoder_1_out0), .out1(decoder_1_out1), .out2(decoder_1_out2), .out3(decoder_1_out3), .sel(waddr));  // open: en
  and and_1 (and_1_out, decoder_1_out0, wen);
  and and_2 (and_2_out, decoder_1_out1, wen);
  and and_3 (and_3_out, decoder_1_out2, wen);
  and and_4 (and_4_out, decoder_1_out3, wen);
  Register A0 (.D(wdata), .en(and_1_out), .clk(clock), .Q(r0_out), .clr(1'b0));
  Register A1 (.D(wdata), .en(and_2_out), .clk(clock), .Q(r1_out), .clr(1'b0));
  Register A2 (.D(wdata), .en(and_3_out), .clk(clock), .Q(r2_out), .clr(1'b0));
  Register A3 (.D(wdata), .en(and_4_out), .clk(clock), .Q(r3_out), .clr(1'b0));
  Multiplexer #(.select(2), .width(8)) multiplexer_1 (
    .in0(r0_out), .in1(r1_out), .in2(r2_out), .in3(r3_out), .out(rdata1), .sel(raddr1));
  Multiplexer #(.select(2), .width(8)) multiplexer_2 (
    .in0(r0_out), .in1(r1_out), .in2(r2_out), .in3(r3_out), .out(rdata2), .sel(raddr2));
endmodule

module decorder24 (
  input  A1,
  input  A0,
  output Y0,
  output Y1,
  output Y2,
  output Y3
);

  wire not_1_out, not_2_out;

  not not_1 (not_1_out, A1);
  not not_2 (not_2_out, A0);
  and and_1 (Y0, not_1_out, not_2_out);
  and and_2 (Y1, A1, not_2_out);
  and and_3 (Y2, not_1_out, A0);
  and and_4 (Y3, A1, A0);
endmodule

module dec (
  input  [7:0] instr,
  output [3:0] offset,
  output [1:0] rs2,
  output [1:0] rs1,
  output [1:0] rd,
  output is_add,
  output is_io,
  output is_li,
  output [1:0] imm,
  output is_bner0,
  output [1:0] s,
  output [2:0] idx,
  output io_dir
);

  Decoder #(.select(2)) decoder_1 (
    .out0(is_add), .out1(is_io), .out2(is_li), .out3(is_bner0), .sel(instr[7:6]));  // open: en

  assign idx = instr[2:0];
  assign imm = instr[1:0];
  assign io_dir = instr[3];
  assign offset = instr[5:2];
  assign rd = instr[5:4];
  assign rs1 = instr[3:2];
  assign rs2 = instr[1:0];
  assign s = instr[3:2];
endmodule

module PC (
  input  [7:0] pc_next,
  input  WE,
  input  clock,
  output [7:0] pc_out
);

  Register register_1 (.D(pc_next), .en(WE), .clk(clock), .Q(pc_out), .clr(1'b0));
endmodule

module ALU (
  input  [7:0] RegA,
  input  [7:0] RegB,
  input  OE,
  output [7:0] result,
  output Carry,
  output [7:0] Dout
);

  Adder adder_1 (.a(RegA), .b(RegB), .out(result), .cin(1'b0), .cout(Carry));
  assign Dout = OE ? result : 8'bz;  // Controlled_Buffer controlled_buffer_1
endmodule

module seg7_rom (
  input  [3:0] in_1,
  output a,
  output b,
  output c,
  output d,
  output e,
  output f,
  output g
);

  ROM #(.addrWidth(4), .dataWidth(7)) rom_1 (.addr(in_1), .data({g, f, e, d, c, b, a}));

  // Notes on the sheet:
  //   contents of rom_1 (hex, n*v repeats v):
  //   7e 30 6d 79 33 5b 5f 70 7f 7b
endmodule
