// Logisim project xor.circ as structural Verilog: 1 circuit, main circuit main
module main (
  input  A,
  input  B,
  output out_3
);

  wire xor_1_out;

  xor xor_1 (xor_1_out, A, B);
endmodule
